# Fritzing sketch rubberband_turret_leonardo (saved by Fritzing 0.9.2b)
breadboards: 1

parts:
  Part1 = Arduino Leonardo (Rev3b)
  U1 = Wiichuck Adapter
  Vertical = Basic Servo
  Horizontal = Basic Servo
  Shooter = Basic Servo
  VCC1 = Battery
  BAT1 = BC9VPC [package=bc9vpc]  # not connected

nets:
  N1: Part1.3V3, U1.+
  GND: Part1.GND, U1.-, Vertical.gnd, Horizontal.gnd, Shooter.gnd, VCC1.-
  N2: Part1.D8/A8, Shooter.pulse
  N3: Part1.D9_PWM/A9, Horizontal.pulse
  N4: Part1.D10_PWM/A10, Vertical.pulse
  N5: Part1.SDA, U1.SDA
  N6: Part1.SCL, U1.SCL
  VCC: Vertical.vcc, Horizontal.vcc, Shooter.vcc, VCC1.+

custom parts:
  Wiichuck Adapter: SCP1000 Barometric Pressure sensor. Can sense air pressure and temperature. SPI interface.
