# Fritzing sketch rubberband_turret_uno (saved by Fritzing 0.9.2b)
breadboards: 1

parts:
  Part1 = Arduino Uno (Rev3)
  VCC1 = Battery
  Y-Axis = Basic Servo
  X-Axis = Basic Servo
  Shooter = Basic Servo
  WiiChuck_Adaptor = Wiichuck Adapter
  BAT1 = BC9VPC [package=bc9vpc]  # not connected

nets:
  N1: Part1.A2, WiiChuck_Adaptor.-
  N2: Part1.A3, WiiChuck_Adaptor.+
  N3: Part1.A4/SDA, WiiChuck_Adaptor.SDA
  N4: Part1.A5/SCL, WiiChuck_Adaptor.SCL
  N5: Part1.D8, Shooter.pulse
  N6: Part1.D9_PWM, X-Axis.pulse
  N7: Part1.D10_PWM/SS, Y-Axis.pulse
  GND: Part1.GND, VCC1.-, Y-Axis.gnd, X-Axis.gnd, Shooter.gnd
  VCC: VCC1.+, Y-Axis.vcc, X-Axis.vcc, Shooter.vcc

custom parts:
  Wiichuck Adapter: SCP1000 Barometric Pressure sensor. Can sense air pressure and temperature. SPI interface.
